// Logisim project computer.circ as structural Verilog: 1 circuit, main circuit main
module main (
);

  wire and_1_out, clock_1_out, not_1_out, not_2_out, undriven, undriven_2, undriven_3, undriven_4,
       undriven_5, undriven_6, undriven_7, undriven_8, undriven_9, undriven_10, undriven_11, undriven_12;
  wire [3:0] controlled_buffer_4_out, controlled_buffer_4_out_2;
  wire [7:0] adder_1_out, controlled_buffer_1_out, controlled_buffer_2_out, controlled_buffer_3_out,
       controlled_buffer_6_out, controlled_buffer_8_out, controlled_buffer_9_out, controlled_buffer_10_out,
       counter_2_q, ram_1_data, register_2_q, register_3_q, register_4_q, subtractor_1_out;

  Clock clock_1 (.out(clock_1_out));
  assign controlled_buffer_1_out = undriven ? {controlled_buffer_4_out_2, controlled_buffer_4_out} : 8'bz;  // Controlled_Buffer controlled_buffer_1
  Register register_1 (.D(controlled_buffer_2_out), .en(1'b1), .clk(and_1_out));  // open: Q, clr
  Counter counter_1 (.clk(and_1_out));  // open: load, D, count, Q, carry, clr
  not not_1 (not_1_out, undriven_3);
  Register register_2 (.D(controlled_buffer_3_out), .Q(register_2_q), .clk(and_1_out));  // open: en, clr
  RAM #(.bus("separate")) ram_1 (
    .addr(register_2_q), .din(controlled_buffer_1_out), .data(ram_1_data), .str(undriven), .sel(1'b1),
    .clk(and_1_out), .ld(undriven_2));  // open: clr
  assign controlled_buffer_2_out = undriven_4 ? {controlled_buffer_4_out_2, controlled_buffer_4_out} : 8'bz;  // Controlled_Buffer controlled_buffer_2
  Hex_Digit_Display hex_digit_display_1 (.value(controlled_buffer_4_out_2));  // open: dp
  and and_1 (and_1_out, not_1_out, clock_1_out);
  assign controlled_buffer_3_out = undriven_5 ? {controlled_buffer_4_out_2, controlled_buffer_4_out} : 8'bz;  // Controlled_Buffer controlled_buffer_3
  assign {controlled_buffer_4_out_2, controlled_buffer_4_out} = undriven_2 ? ram_1_data : 8'bz;  // Controlled_Buffer controlled_buffer_4
  ROM rom_1 ();  // open: addr, data, sel
  Hex_Digit_Display hex_digit_display_2 (.value(controlled_buffer_4_out));  // open: dp
  assign {controlled_buffer_4_out_2, controlled_buffer_4_out} = undriven_6 ? controlled_buffer_10_out : 8'bz;  // Controlled_Buffer controlled_buffer_5
  assign controlled_buffer_6_out = undriven_7 ? {controlled_buffer_4_out_2, controlled_buffer_4_out} : 8'bz;  // Controlled_Buffer controlled_buffer_6
  assign {controlled_buffer_4_out_2, controlled_buffer_4_out} = undriven_9 ? counter_2_q : 8'bz;  // Controlled_Buffer controlled_buffer_7
  assign controlled_buffer_8_out = undriven_12 ? {controlled_buffer_4_out_2, controlled_buffer_4_out} : 8'bz;  // Controlled_Buffer controlled_buffer_8
  assign controlled_buffer_9_out = undriven_8 ? {controlled_buffer_4_out_2, controlled_buffer_4_out} : 8'bz;  // Controlled_Buffer controlled_buffer_9
  Counter counter_2 (
    .D(controlled_buffer_8_out), .count(undriven_10), .Q(counter_2_q), .clk(and_1_out));  // open: load, carry, clr
  Register register_3 (.D(controlled_buffer_9_out), .en(1'b1), .Q(register_3_q), .clk(and_1_out));  // open: clr
  assign controlled_buffer_10_out = not_2_out ? adder_1_out : 8'bz;  // Controlled_Buffer controlled_buffer_10
  Adder adder_1 (.a(register_3_q), .b(register_4_q), .out(adder_1_out));  // open: cin, cout
  Register register_4 (.D(controlled_buffer_6_out), .en(1'b1), .Q(register_4_q), .clk(and_1_out));  // open: clr
  Subtractor subtractor_1 (.a(register_3_q), .b(register_4_q), .out(subtractor_1_out));  // open: bin, bout
  not not_2 (not_2_out, undriven_11);
  assign controlled_buffer_10_out = undriven_11 ? subtractor_1_out : 8'bz;  // Controlled_Buffer controlled_buffer_11

  // Notes on the sheet:
  //   RAM
  //   Memory Register
  //   Input Register
  //   Clock
  //   Adder
  //   Program Counter
  //   A Register
  //   B register
  //   II
  //   MI
  //   SUB
  //   MO
  //   MA
  //   EO
  //   AI
  //   CE
  //   BI
  //   CI
  //   CO
  //   HLT
endmodule
